# Fritzing sketch PiT-Single-v1.0-Chinese-4pin-sensor-v1.1 (saved by Fritzing 0.9.3b)
breadboards: 1

parts:
  Raspberry_Pi_1 = Raspberry Pi 3 [part_number=RPI-3-V1.2]
  M1 = BME280

nets:
  3V3: Raspberry_Pi_1.3v3, M1.VIN
  N1: Raspberry_Pi_1.GPIO2, M1.SDA
  N2: Raspberry_Pi_1.GPIO3, M1.SCL
  GND: Raspberry_Pi_1.GND, M1.GND

custom parts:
  BME280: Temperature Humidity Barometric presure Sensor
